// Logisim project hack.circ as structural Verilog: 9 circuits, main circuit main
module main (
  input  M3,
  input  M2,
  input  M1,
  input  M0,
  output out_5,
  output [3:0] out_6,
  output [3:0] out_7
);

  wire encoder_1_encoder_o, piso_1_piso_o;

  PISO piso_1 (.M3(M3), .M2(M2), .M1(M1), .M0(M0), .E(1'b0), .R(1'b0), .piso_o(piso_1_piso_o));
  encoder encoder_1 (.encoder_in(piso_1_piso_o), .E(1'b0), .encoder_o(encoder_1_encoder_o));
  noisy_channel noisy_channel_1 (.ip(encoder_1_encoder_o), .op(out_5), .seq_PN(out_6), .upCounter(out_7));
endmodule

module encoder (
  input  encoder_in,
  input  E,
  output encoder_o
);

  wire and_1_out, and_2_out, clock_1_out, d_ff_1_q, d_ff_2_q, d_ff_3_q, not_1_out, or_1_out, xor_1_out,
       xor_2_out;

  Clock clock_1 (.out(clock_1_out));
  D_Flip_Flop d_ff_1 (.D(encoder_in), .clk(clock_1_out), .Q(d_ff_1_q));  // open: Qn, preset, reset
  D_Flip_Flop d_ff_2 (.D(d_ff_1_q), .clk(clock_1_out), .Q(d_ff_2_q));  // open: Qn, preset, reset
  // Probe on xor_1_out
  xor xor_1 (xor_1_out, encoder_in, d_ff_2_q);
  // Probe on xor_2_out
  ExactlyOne xor_2 (.out(xor_2_out), .in0(d_ff_2_q), .in1(d_ff_1_q), .in2(encoder_in));
  not not_1 (not_1_out, E);
  D_Flip_Flop d_ff_3 (.D(xor_1_out), .clk(clock_1_out), .Q(d_ff_3_q), .reset(1'b0));  // open: Qn, preset
  and and_1 (and_1_out, d_ff_3_q, E);
  and and_2 (and_2_out, not_1_out, xor_2_out);
  or or_1 (or_1_out, and_1_out, and_2_out);
  D_Flip_Flop d_ff_4 (.D(or_1_out), .clk(clock_1_out), .Q(encoder_o), .reset(1'b0));  // open: Qn, preset
endmodule

module PISO (
  input  M3,
  input  M2,
  input  M1,
  input  M0,
  input  E,
  input  R,
  output piso_o
);

  wire and_1_out, and_2_out, and_3_out, and_4_out, and_5_out, and_6_out, clock_1_out, d_ff_1_q, d_ff_2_q,
       d_ff_3_q, not_1_out, or_1_out, or_2_out, or_3_out;

  not not_1 (not_1_out, E);
  Clock clock_1 (.out(clock_1_out));
  D_Flip_Flop d_ff_1 (.D(M3), .clk(clock_1_out), .Q(d_ff_1_q), .reset(R));  // open: Qn, preset
  and and_1 (and_1_out, d_ff_1_q, E);
  and and_2 (and_2_out, not_1_out, M2);
  or or_1 (or_1_out, and_1_out, and_2_out);
  D_Flip_Flop d_ff_2 (.D(or_1_out), .clk(clock_1_out), .Q(d_ff_2_q), .reset(R));  // open: Qn, preset
  and and_3 (and_3_out, d_ff_2_q, E);
  and and_4 (and_4_out, not_1_out, M1);
  or or_2 (or_2_out, and_3_out, and_4_out);
  D_Flip_Flop d_ff_3 (.D(or_2_out), .clk(clock_1_out), .Q(d_ff_3_q), .reset(R));  // open: Qn, preset
  and and_5 (and_5_out, d_ff_3_q, E);
  and and_6 (and_6_out, not_1_out, M0);
  or or_3 (or_3_out, and_5_out, and_6_out);
  D_Flip_Flop d_ff_4 (.D(or_3_out), .clk(clock_1_out), .Q(piso_o), .reset(R));  // open: Qn, preset
endmodule

module PN_Seq (
  input  en,
  output q3,
  output q2,
  output q1,
  output q0
);

  wire and_1_out, and_2_out, and_3_out, and_4_out, and_5_out, and_6_out, and_7_out, and_8_out, and_9_out,
       and_10_out, and_11_out, and_12_out, and_13_out, and_14_out, clk_out, not_1_out, not_2_out, not_3_out,
       not_4_out, or_1_out, or_2_out, or_3_out, or_4_out, or_5_out;

  not not_1 (not_1_out, q3);
  not not_2 (not_2_out, q2);
  not not_3 (not_3_out, q1);
  not not_4 (not_4_out, q0);
  and and_1 (and_1_out, q3, not_3_out);
  and and_2 (and_2_out, q2, q1, not_4_out);
  and and_3 (and_3_out, not_1_out, not_2_out, q1, q0);
  or or_1 (or_1_out, and_1_out, and_2_out, and_3_out);
  Clock clk (.out(clk_out));
  D_Flip_Flop A (.D(or_1_out), .clk(and_4_out), .Q(q3));  // open: Qn, preset, reset
  and and_4 (and_4_out, clk_out, en);
  and and_5 (and_5_out, q3, q1);
  and and_6 (and_6_out, not_1_out, not_2_out, not_4_out);
  and and_7 (and_7_out, not_2_out, not_3_out, q0);
  and and_8 (and_8_out, not_2_out, q1, not_4_out);
  and and_9 (and_9_out, q3, not_3_out);
  and and_10 (and_10_out, q2, not_3_out, not_4_out);
  and and_11 (and_11_out, q2, not_3_out);
  and and_12 (and_12_out, not_2_out, q1, q0);
  and and_13 (and_13_out, not_1_out, not_2_out, q1);
  and and_14 (and_14_out, q3, not_3_out, not_4_out);
  or or_2 (or_2_out, and_5_out, and_6_out);
  or or_3 (or_3_out, and_7_out, and_8_out, and_9_out);
  or or_4 (or_4_out, and_11_out, and_12_out, and_13_out, and_14_out);
  D_Flip_Flop B (.D(or_2_out), .clk(and_4_out), .Q(q2));  // open: Qn, preset, reset
  or or_5 (or_5_out, or_3_out, and_10_out);
  D_Flip_Flop C (.D(or_5_out), .clk(and_4_out), .Q(q1));  // open: Qn, preset, reset
  D_Flip_Flop D (.D(or_4_out), .clk(and_4_out), .Q(q0));  // open: Qn, preset, reset

  // Notes on the sheet:
  //   A
  //   B
  //   C
  //   D
endmodule

module noisy_channel (
  input  ip,
  output op,
  output [3:0] seq_PN,
  output [3:0] upCounter
);

  wire clock_1_out, comp_1_op, d_ff_1_q, not_1_out;

  upcon upcon_1 (.R(d_ff_1_q), .q0(upCounter[0]), .q1(upCounter[1]), .q2(upCounter[2]), .q3(upCounter[3]));
  not not_1 (not_1_out, ip);
  PN_Seq pn_seq_1 (.en(d_ff_1_q), .q3(seq_PN[3]), .q2(seq_PN[2]), .q1(seq_PN[1]), .q0(seq_PN[0]));
  comp comp_1 (
    .p3(seq_PN[3]), .p2(seq_PN[2]), .p1(seq_PN[1]), .p0(seq_PN[0]), .u0(upCounter[0]), .u1(upCounter[1]),
    .u2(upCounter[2]), .u3(upCounter[3]), .op(comp_1_op));
  mux mux_1 (.A(ip), .B(not_1_out), .S(d_ff_1_q), .op(op));
  D_Flip_Flop d_ff_1 (.D(comp_1_op), .clk(clock_1_out), .Q(d_ff_1_q));  // open: Qn, preset, reset
  Clock clock_1 (.out(clock_1_out));
endmodule

module mux (
  input  A,
  input  B,
  input  S,
  output op
);

  wire and_1_out, and_2_out, not_1_out;

  not not_1 (not_1_out, S);
  and and_1 (and_1_out, A, not_1_out);
  and and_2 (and_2_out, S, B);
  or or_1 (op, and_1_out, and_2_out);
endmodule

module comp (
  input  p3,
  input  p2,
  input  p1,
  input  p0,
  input  u0,
  input  u1,
  input  u2,
  input  u3,
  output op
);

  wire xnor_1_out, xnor_2_out, xnor_3_out, xnor_4_out;

  xnor xnor_1 (xnor_1_out, p0, u0);
  xnor xnor_2 (xnor_2_out, p1, u1);
  xnor xnor_3 (xnor_3_out, p2, u2);
  xnor xnor_4 (xnor_4_out, p3, u3);
  and and_1 (op, xnor_1_out, xnor_2_out, xnor_3_out, xnor_4_out);
endmodule

module upcon (
  input  R,
  output q0,
  output q1,
  output q2,
  output q3
);

  wire and_1_out, and_2_out, clock_1_out;

  Clock clock_1 (.out(clock_1_out));
  J_K_Flip_Flop j_k_ff_1 (.J(1'b1), .K(1'b1), .clk(clock_1_out), .Q(q0), .reset(R));  // open: Qn, preset
  J_K_Flip_Flop j_k_ff_2 (.J(q0), .K(q0), .clk(clock_1_out), .Q(q1), .reset(R));  // open: Qn, preset
  and and_1 (and_1_out, q0, q1);
  J_K_Flip_Flop j_k_ff_3 (.J(and_1_out), .K(and_1_out), .clk(clock_1_out), .Q(q2), .reset(R));  // open: Qn, preset
  and and_2 (and_2_out, and_1_out, q2);
  J_K_Flip_Flop j_k_ff_4 (.J(and_2_out), .K(and_2_out), .clk(clock_1_out), .Q(q3), .reset(R));  // open: Qn, preset
endmodule

module BMU (
  input  a0,
  input  b0,
  input  in_3,
  input  in_4,
  input  in_5,
  input  in_6,
  input  in_7,
  input  in_8,
  input  in_9,
  input  in_10,
  input  in_11,
  input  in_12,
  input  in_13,
  input  in_14,
  input  in_15,
  input  in_16
);

  wire and_1_out, and_2_out, and_3_out, and_4_out, not_1_out, not_2_out, not_3_out, not_4_out, xor_1_out,
       xor_2_out, xor_3_out, xor_4_out, xor_5_out, xor_6_out, xor_7_out, xor_8_out;

  xor xor_1 (xor_1_out, a0, b0);
  xor xor_2 (xor_2_out, in_3, in_4);
  xor xor_3 (xor_3_out, in_5, in_6);
  xor xor_4 (xor_4_out, in_7, in_8);
  xor xor_5 (xor_5_out, in_9, in_10);
  xor xor_6 (xor_6_out, in_11, in_12);
  xor xor_7 (xor_7_out, in_13, in_14);
  xor xor_8 (xor_8_out, in_15, in_16);
  and and_1 (and_1_out, xor_1_out, xor_2_out);
  not not_1 (not_1_out, and_1_out);
  and and_2 (and_2_out, xor_3_out, xor_4_out);
  not not_2 (not_2_out, and_2_out);
  and and_3 (and_3_out, xor_5_out, xor_6_out);
  not not_3 (not_3_out, and_3_out);
  and and_4 (and_4_out, xor_7_out, xor_8_out);
  not not_4 (not_4_out, and_4_out);
endmodule
